# Fritzing sketch digital_temperature_with_i2c_lcd (saved by Fritzing 0.9.3b)
breadboards: 1

parts:
  U1 = PCF8574 [package="DIP16 [THT]"]
  R1 = Temperature Sensor (Thermistor) [thermistor_type=NTC package=THT]
  R2 = Resistor [tolerance=±5% resistance=10k package=THT]
  LCD1 = LCD screen
  R3 = Rotary Potentiometer (Small) [maximum_resistance=100kΩ package=THT]
  Arduino1 = Arduino Uno (Rev3)

nets:
  GND: U1.A0, U1.A3, U1.GND, R2.Pin_1, LCD1.VSS, LCD1.LED-, R3.leg1, Arduino1.GND
  N1: U1.P0, LCD1.DB4
  N2: U1.P1, LCD1.DB5
  N3: U1.P2, LCD1.DB6
  N4: U1.P3, LCD1.DB7
  N5: U1.P4, LCD1.E
  N6: U1.P5, LCD1.R/W
  N7: U1.P6, LCD1.RS
  VCC: U1.VCC, R1.pin_0, LCD1.VDD, LCD1.LED+, R3.leg2
  N8: R1.pin_1, R2.Pin_0, Arduino1.A0
  N9: LCD1.V0, R3.wiper
